# Fritzing sketch shield_esp32_grove (saved by Fritzing 1.0.3b)
circuit board: 7.77488cm x 4.93671cm
breadboards: 2

parts:
  M1 = DOIT Esp32 DevKit v1 (30 pins long, 11 pins width) [part_number=ESP32S-PIN30]
  J3 = double row female pin header, 30 pins [form="♀ (female)"]
  i2c1 = female pin header, 4 pins [form="♀ (female)"]
  i2c2 = female pin header, 4 pins [form="♀ (female)"]
  hx711 = female pin header, 4 pins [form="♀ (female)"]
  d13 = female pin header, 4 pins [form="♀ (female)"]
  J2 = double row female pin header, 30 pins [form="♀ (female)"]
  analog = female pin header, 4 pins [form="♀ (female)"]

nets:
  N1: M1.3V3, i2c1.pin3, i2c2.pin3, hx711.pin3, d13.pin3, J2.pin1, J2.pin30, analog.pin3
  N2: M1.GND, J3.pin2, J3.pin29, i2c1.pin4, i2c2.pin4, hx711.pin4, d13.pin4, J2.pin2, J2.pin29, analog.pin4
  N3: M1.D15, J2.pin3
  N4: M1.D2, J2.pin4
  N5: M1.D4, hx711.pin2, J2.pin5
  N6: M1.RX2, J2.pin6
  N7: M1.TX2, J2.pin7
  N8: M1.D5, J2.pin8
  N9: M1.D18, J2.pin9
  N10: M1.D19, J2.pin10
  N11: M1.D21, i2c1.pin2, i2c2.pin2, J2.pin11
  N12: M1.RX0, J2.pin12
  N13: M1.TX0, J2.pin13, J2.pin18
  N14: M1.D22, i2c1.pin1, i2c2.pin1, J2.pin14
  N15: M1.D23, J2.pin15
  N16: M1.D32, J3.pin10, J3.pin21, analog.pin2
  N17: M1.D33, J3.pin9, J3.pin22, analog.pin1
  N18: M1.D12, J3.pin4, J3.pin27, hx711.pin1
  N19: M1.D13, J3.pin3, J3.pin28, d13.pin1
  N20: M1.VIN, J3.pin1, J3.pin30
  N21: J3.pin5, J3.pin26
  N22: J3.pin6, J3.pin25
  N23: J3.pin7, J3.pin24
  N24: J3.pin8, J3.pin23
  N25: J3.pin11, J3.pin20
  N26: J3.pin12, J3.pin19
  N27: J3.pin13, J3.pin18
  N28: J3.pin14, J3.pin17
  N29: J3.pin15, J3.pin16

custom parts:
  DOIT Esp32 DevKit v1 (30 pins long, 11 pins width): The DOIT Esp32 DevKit v1 is one of the development board created by DOIT to evaluate the ESP-WROOM-32 module. It is based on the ESP32 microcontroller that boasts Wifi, Bluetooth, Ethernet and Low Power support all in a single chip. (vanepp) made breadboard work, adjusted pin numbering and labels and reduced size of schematic and cleaned up pcb. This chip is 30pins long (2 x15) and 11 pins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
